# Fritzing sketch RailCarRFID_ArduinoMega (saved by Fritzing 1.0.1rc)

parts:
  IC2 = ZS-X11H [chip_label=IC package="DIP (Dual Inline) [THT]"]
  Componente1 = Arduino Mega 2560 (Rev3)
  W5500_Module1 = W5500 Ethernet module [package="DIP (Dual Inline) [THT]"]
  Componente2 = RFID-RC522-v3
  LCM1602_IIC1 = LCM1602 IIC [part_number="LCM1602 IIC" chip_label="LCM1602 IIC" package="DIP (Dual Inline) [THT]"]
  LCD1 = LCD screen [mn=s]
  R1 = Resistor [tolerance=±5% power=0.25W resistance=220 package=THT]
  R2 = Resistor [tolerance=±5% power=0.25W resistance=220 package=THT]
  R3 = Resistor [tolerance=±5% power=0.25W resistance=220 package=THT]
  A1 = hub motor wheel
  IC4 = BATTERY PACK [package="DIP (Dual Inline) [THT]"]
  LED1 = RGB LED (com. anode, rbg) [color="Red (633nm)" current=0.030A package="5 mm [THT]"]
  S2 = Round Pushbutton

nets:
  N1: IC2.MA, A1.Pin_1
  N2: IC2.MB, A1.Pin_2
  N3: IC2.MC, A1.Pin_3
  VCC: IC2.VCC, IC4.VCC
  N4: IC2.GND#4, IC4.GND
  N5: IC2.CTRL, Componente1.D3_PWM
  GND: IC2.GND#7, Componente1.GND, W5500_Module1.GND, Componente2.GND, LCM1602_IIC1.GND, S2.leg0
  N6: IC2.DIR, Componente1.D2_PWM
  N7: IC2.GND#16, A1.Pin_8
  N8: IC2.Hc, A1.Pin_7
  N9: IC2.Hb, A1.Pin_6
  N10: IC2.Ha, A1.Pin_5
  N11: IC2.5V, A1.Pin_4
  N12: Componente1.D21/SCL, LCM1602_IIC1.SCL
  N13: Componente1.D20/SDA, LCM1602_IIC1.SDA
  N14: Componente1.D9_PWM, Componente2.RST
  N15: Componente1.D8_PWM, S2.leg1
  3V3: Componente1.3V3, Componente2.3.3V
  5V: Componente1.5V, W5500_Module1.5V, LCM1602_IIC1.VCC, LED1.common_anode
  N16: Componente1.D4_PWM, R3.Pin_1
  N17: Componente1.D5_PWM, R2.Pin_1
  N18: Componente1.D6_PWM, R1.Pin_1
  N19: Componente1.D7_PWM, W5500_Module1.RST
  N20: Componente1.D50, W5500_Module1.MISO, Componente2.MISO
  N21: Componente1.D51, W5500_Module1.MOSI, Componente2.MOSI
  N22: Componente1.D52, W5500_Module1.SCLK, Componente2.SCK
  N23: Componente1.D53, W5500_Module1.SCS, Componente2.SDA
  VSS: LCM1602_IIC1.VSS, LCD1.VSS
  VDD: LCM1602_IIC1.VDD, LCD1.VDD
  N24: LCM1602_IIC1.V0, LCD1.V0
  N25: LCM1602_IIC1.RS, LCD1.RS
  N26: LCM1602_IIC1.RW, LCD1.R/W
  N27: LCM1602_IIC1.E, LCD1.E
  N28: LCM1602_IIC1.D0, LCD1.DB0
  N29: LCM1602_IIC1.D1, LCD1.DB1
  N30: LCM1602_IIC1.D2, LCD1.DB2
  N31: LCM1602_IIC1.D3, LCD1.DB3
  N32: LCM1602_IIC1.D4, LCD1.DB4
  N33: LCM1602_IIC1.D5, LCD1.DB5
  N34: LCM1602_IIC1.D6, LCD1.DB6
  N35: LCM1602_IIC1.D7, LCD1.DB7
  N36: LCM1602_IIC1.A, LCD1.LED+
  N37: LCM1602_IIC1.K, LCD1.LED-
  N38: R1.Pin_0, LED1.red_cathode
  N39: R2.Pin_0, LED1.green_cathode
  N40: R3.Pin_0, LED1.blue_cathode

notes:
  Battery

custom parts:
  ZS-X11H: A BLDC controller
  W5500 Ethernet module: W5500 based SPI Ethernet module for Arduino, etc.
  RFID-RC522-v3: A simple China made RFID-RC522 Reader (6x4 cm); do check the pin labels, as this is a MFRC522 based clone.
  LCM1602 IIC: I2C-Module to use a 1602 or 2004 LCD on with the wire.h libory Serial LCD Modul
